// Logisim project exp6-1a.circ as structural Verilog: 1 circuit, main circuit main
module main (
  input  A,
  input  B,
  input  C
);

  wire and_1_out, and_2_out, and_3_out, not_1_out, not_2_out, not_3_out, or_1_out;

  not not_1 (not_1_out, A);
  not not_2 (not_2_out, B);
  not not_3 (not_3_out, C);
  and and_1 (and_1_out, C, not_2_out, not_1_out);
  and and_2 (and_2_out, not_1_out, B, not_3_out);
  or or_1 (or_1_out, and_1_out, and_2_out, and_3_out);
  and and_3 (and_3_out, A, B, not_3_out);

  // Notes on the sheet:
  //   Luke Ward
  //   Sec 1
  //   Exp 6
  //   1a
endmodule
