// Logisim project exp6-1b.circ as structural Verilog: 1 circuit, main circuit main
module main (
  input  [2:0] ABC
);

  wire decoder_1_out0, decoder_1_out1, decoder_1_out2, decoder_1_out3, decoder_1_out4, decoder_1_out5,
       decoder_1_out6, decoder_1_out7, or_1_out;

  Decoder #(.select(3), .tristate("false")) decoder_1 (
    .out0(decoder_1_out0), .out1(decoder_1_out1), .out2(decoder_1_out2), .out3(decoder_1_out3),
    .out4(decoder_1_out4), .out5(decoder_1_out5), .out6(decoder_1_out6), .out7(decoder_1_out7), .sel(ABC));
  or or_1 (or_1_out, decoder_1_out1, decoder_1_out2, decoder_1_out6);

  // Notes on the sheet:
  //   Luke Ward
  //   Sec 1
  //   Exp 6
  //   1b
endmodule
