// Logisim project exp6-1c.circ as structural Verilog: 1 circuit, main circuit main
module main (
  input  in_1,
  input  in_2,
  input  [2:0] in_3
);

  wire multiplexer_1_out, undriven, undriven_2, undriven_3;

  Multiplexer #(.select(3), .width(1)) multiplexer_1 (
    .in0(in_1), .in1(undriven), .in2(in_1), .in3(in_1), .in4(in_1), .in5(undriven_2), .in6(in_1),
    .in7(undriven_3), .out(multiplexer_1_out), .sel(in_3));

  // Notes on the sheet:
  //   Luke Ward
  //   Sec 1
  //   Exp 6
  //   1c
endmodule
